// Logisim project muxrisccore.circ as structural Verilog: 1 circuit, main circuit main
module main (
);

  wire clock_1_out, clock_2_out, clock_3_out, clock_4_out, clock_5_out, comparator_1_eq, comparator_2_eq,
       comparator_3_eq, controlled_buffer_1_out, multiplexer_2_out, not_1_out, or_1_out, register_3_q,
       xor_1_out;
  wire [1:0] bitselector_1_out, register_1_q;
  wire [15:0] bitselector_2_out, counter_1_q, multiplexer_1_out;
  wire [63:0] multiplexer_3_out, ram_1_dout;

  Register #(.trigger("falling"), .width(2)) register_1 (
    .D(bitselector_1_out), .en(not_1_out), .clk(clock_1_out), .Q(register_1_q));  // open: clr
  BitSelector #(.group(2), .width(64)) bitselector_1 (.in(ram_1_dout), .out(bitselector_1_out), .sel({5{1'b0}}));
  not not_1 (not_1_out, register_3_q);
  Clock clock_1 (.out(clock_1_out));
  Comparator #(.width(2)) comparator_1 (.a(register_1_q), .b(2'b00), .eq(comparator_1_eq));  // open: gt, lt
  or or_1 (or_1_out, comparator_1_eq, comparator_2_eq);
  Comparator #(.width(2)) comparator_2 (.a(register_1_q), .b(2'b01), .eq(comparator_2_eq));  // open: gt, lt
  assign controlled_buffer_1_out = or_1_out ? register_3_q : 1'bz;  // Controlled_Buffer controlled_buffer_1
  BitSelector #(.group(16), .width(64)) bitselector_2 (.in(ram_1_dout), .out(bitselector_2_out), .sel(2'b00));
  Counter #(.max('hffff), .trigger("falling"), .width(16)) counter_1 (
    .load(controlled_buffer_1_out), .D(bitselector_2_out), .count(or_1_out), .Q(counter_1_q),
    .clk(clock_2_out));  // open: carry, up, clr
  Clock clock_2 (.out(clock_2_out));
  Multiplexer #(.select(2), .width(16)) multiplexer_1 (
    .in0(counter_1_q), .in1(counter_1_q), .out(multiplexer_1_out), .sel(register_1_q));  // open: in2, in3
  Multiplexer #(.select(2)) multiplexer_2 (
    .in0(1'b0), .in1(1'b0), .out(multiplexer_2_out), .sel(register_1_q));  // open: in2, in3
  RAM #(.addrWidth(16), .dataWidth(64), .enables("line"), .\type ("nonvolatile")) ram_1 (
    .addr(multiplexer_1_out), .we(multiplexer_2_out), .clk(clock_3_out), .din(multiplexer_3_out),
    .dout(ram_1_dout));
  Clock clock_3 (.out(clock_3_out));
  Multiplexer #(.select(2), .width(64)) multiplexer_3 (
    .out(multiplexer_3_out), .sel(register_1_q));  // open: in0, in1, in2, in3
  Register register_2 (.clk(clock_4_out));  // open: D, en, Q, clr
  Clock clock_4 (.out(clock_4_out));
  Comparator #(.width(2)) comparator_3 (.a(register_1_q), .b(2'b01), .eq(comparator_3_eq));  // open: gt, lt
  Register #(.width(1)) register_3 (.D(xor_1_out), .en(1'b1), .clk(clock_5_out), .Q(register_3_q));  // open: clr
  xor xor_1 (xor_1_out, register_3_q, comparator_3_eq);
  Clock clock_5 (.out(clock_5_out));
endmodule
